# Fritzing sketch PC-O-Meter - Fritzing Diagram (saved by Fritzing 0.9.2b)
circuit board: 8.46667cm x 5.64444cm
breadboards: 1

parts:
  Part1 = Photon
  J3 = Basic Servo

nets:
  N1: Part1.A4, J3.pulse
  GND: Part1.GND, J3.gnd
  VIN: Part1.VIN, J3.vcc
